// Logisim project Exponent.circ as structural Verilog: 5 circuits, main circuit main
module main (
  input  [31:0] A,
  input  [31:0] B,
  output [31:0] Sum,
  output [11:0] Exponent,
  output Sign_bit,
  output Zero_Flag
);

  wire exponent_handler_1_decision__if_x___y, exponent_handler_1_decision__if_x_y, not_1_out, not_2_out;
  wire [11:0] exponent_handler_1_difference, exponent_handler_1_larger_exponent;
  wire [26:26] multiplexer_3_out;
  wire [30:0] _32_bit_ALU_output;
  wire [31:0] Fraction_Aligner_modified_number, multiplexer_1_out, multiplexer_2_out, negator_1_out,
       sign_handler_1_out_4, sign_handler_2_out_4;

  exponent_handler exponent_handler_1 (
    .X(A[30:19]), .Y(B[30:19]), .Decision__if_x___y(exponent_handler_1_decision__if_x___y),
    .Decision__If_X_Y(exponent_handler_1_decision__if_x_y),
    .Larger_Exponent(exponent_handler_1_larger_exponent), .Difference(exponent_handler_1_difference));
  not not_1 (not_1_out, exponent_handler_1_decision__if_x_y);
  Multiplexer #(.width(32), .disabled(0), .enable("false")) multiplexer_1 (
    .in0(A), .in1(B), .out(multiplexer_1_out), .sel(not_1_out));
  fraction_allignment_main Fraction_Aligner (
    .Smaller_number(multiplexer_1_out), .Larger_Exp(exponent_handler_1_larger_exponent),
    .Exponent_difference(exponent_handler_1_difference),
    .Modified_number({Fraction_Aligner_modified_number[31], Exponent, Fraction_Aligner_modified_number[18:0]}));
  not not_2 (not_2_out, exponent_handler_1_decision__if_x___y);
  Multiplexer #(.width(32), .disabled(0), .enable("false")) multiplexer_2 (
    .in0(A), .in1(B), .out(multiplexer_2_out), .sel(exponent_handler_1_decision__if_x_y));
  Multiplexer #(.disabled(0), .enable("false")) multiplexer_3 (
    .in0(1'b0), .in1(1'b1), .out(multiplexer_3_out[26]), .sel(not_2_out));
  BitFinder #(.width(32)) bitfinder_1 (.in({Sign_bit, _32_bit_ALU_output}), .found(Zero_Flag));  // open: index
  sign_handler sign_handler_1 (
    .number({6'b000001, multiplexer_2_out[18:0], {7{1'b0}}}), .exp(multiplexer_2_out[30:19]),
    .sign(multiplexer_2_out[31]), .out_4(sign_handler_1_out_4));
  _32_Bit_ALU_main _32_bit_ALU (
    .Input1(sign_handler_1_out_4), .Input2(sign_handler_2_out_4), .c(3'b100),
    .Output({Sign_bit, _32_bit_ALU_output}));  // open: out_5
  sign_handler sign_handler_2 (
    .number({{5{1'b0}}, multiplexer_3_out[26], Fraction_Aligner_modified_number[18:0], {7{1'b0}}}),
    .exp(Exponent), .sign(Fraction_Aligner_modified_number[31]), .out_4(sign_handler_2_out_4));
  Negator #(.width(32)) negator_1 (.in({Sign_bit, _32_bit_ALU_output}), .out(negator_1_out));
  Multiplexer #(.width(32), .enable("false")) multiplexer_4 (
    .in0({Sign_bit, _32_bit_ALU_output}), .in1(negator_1_out), .out(Sum), .sel(Sign_bit));
endmodule

module _1_Bit_ALU (
  input  in_1,
  input  in_2,
  input  C_in,
  input  B_Invert,
  input  Less,
  input  [1:0] ALU_Op,
  output ALU_Output,
  output Set,
  output C_out
);

  wire and_1_out, multiplexer_1_out, not_1_out, or_1_out;

  not not_1 (not_1_out, in_1);
  Multiplexer #(.enable("false")) multiplexer_1 (.in0(in_1), .in1(not_1_out), .out(multiplexer_1_out), .sel(B_Invert));
  and and_1 (and_1_out, in_2, in_1);
  or or_1 (or_1_out, in_2, in_1);
  Adder #(.width(1)) adder_1 (.a(in_2), .b(multiplexer_1_out), .out(Set), .cin(C_in), .cout(C_out));
  Multiplexer #(.select(2), .enable("false")) multiplexer_2 (
    .in0(and_1_out), .in1(or_1_out), .in2(Set), .in3(Less), .out(ALU_Output), .sel(ALU_Op));
endmodule

module _16_Bit_ALU (
  input  B_Invert,
  input  [15:0] A,
  input  [15:0] B,
  output Zero_Flag,
  output [15:0] ALU_Output,
  output Overflow_Flag,
  output C_Out
);

  wire n1_bit_alu_1_c_out, n1_bit_alu_2_c_out, n1_bit_alu_3_c_out, n1_bit_alu_4_c_out, n1_bit_alu_5_c_out,
       n1_bit_alu_6_c_out, n1_bit_alu_7_c_out, n1_bit_alu_8_c_out, n1_bit_alu_9_c_out, n1_bit_alu_10_c_out,
       n1_bit_alu_11_c_out, n1_bit_alu_12_c_out, n1_bit_alu_13_c_out, n1_bit_alu_14_c_out,
       n1_bit_alu_15_c_out, n1_bit_alu_16_set;

  _1_Bit_ALU u_1_bit_alu_1 (
    .C_in(B_Invert), .Less(n1_bit_alu_16_set), .ALU_Output(ALU_Output[0]), .C_out(n1_bit_alu_1_c_out),
    .in_1(B[0]), .in_2(A[0]), .B_Invert(B_Invert), .ALU_Op(2'b10));  // open: Set
  _1_Bit_ALU u_1_bit_alu_2 (
    .C_in(n1_bit_alu_1_c_out), .Less(1'b0), .ALU_Output(ALU_Output[1]), .C_out(n1_bit_alu_2_c_out),
    .in_1(B[1]), .in_2(A[1]), .B_Invert(B_Invert), .ALU_Op(2'b10));  // open: Set
  _1_Bit_ALU u_1_bit_alu_3 (
    .C_in(n1_bit_alu_2_c_out), .Less(1'b0), .ALU_Output(ALU_Output[2]), .C_out(n1_bit_alu_3_c_out),
    .in_1(B[2]), .in_2(A[2]), .B_Invert(B_Invert), .ALU_Op(2'b10));  // open: Set
  _1_Bit_ALU u_1_bit_alu_4 (
    .C_in(n1_bit_alu_3_c_out), .Less(1'b0), .ALU_Output(ALU_Output[3]), .C_out(n1_bit_alu_4_c_out),
    .in_1(B[3]), .in_2(A[3]), .B_Invert(B_Invert), .ALU_Op(2'b10));  // open: Set
  _1_Bit_ALU u_1_bit_alu_5 (
    .C_in(n1_bit_alu_4_c_out), .Less(1'b0), .ALU_Output(ALU_Output[4]), .C_out(n1_bit_alu_5_c_out),
    .in_1(B[4]), .in_2(A[4]), .B_Invert(B_Invert), .ALU_Op(2'b10));  // open: Set
  _1_Bit_ALU u_1_bit_alu_6 (
    .C_in(n1_bit_alu_5_c_out), .Less(1'b0), .ALU_Output(ALU_Output[5]), .C_out(n1_bit_alu_6_c_out),
    .in_1(B[5]), .in_2(A[5]), .B_Invert(B_Invert), .ALU_Op(2'b10));  // open: Set
  _1_Bit_ALU u_1_bit_alu_7 (
    .C_in(n1_bit_alu_6_c_out), .Less(1'b0), .ALU_Output(ALU_Output[6]), .C_out(n1_bit_alu_7_c_out),
    .in_1(B[6]), .in_2(A[6]), .B_Invert(B_Invert), .ALU_Op(2'b10));  // open: Set
  _1_Bit_ALU u_1_bit_alu_8 (
    .C_in(n1_bit_alu_7_c_out), .Less(1'b0), .ALU_Output(ALU_Output[7]), .C_out(n1_bit_alu_8_c_out),
    .in_1(B[7]), .in_2(A[7]), .B_Invert(B_Invert), .ALU_Op(2'b10));  // open: Set
  _1_Bit_ALU u_1_bit_alu_9 (
    .C_in(n1_bit_alu_8_c_out), .Less(1'b0), .ALU_Output(ALU_Output[8]), .C_out(n1_bit_alu_9_c_out),
    .in_1(B[8]), .in_2(A[8]), .B_Invert(B_Invert), .ALU_Op(2'b10));  // open: Set
  _1_Bit_ALU u_1_bit_alu_10 (
    .C_in(n1_bit_alu_9_c_out), .Less(1'b0), .ALU_Output(ALU_Output[9]), .C_out(n1_bit_alu_10_c_out),
    .in_1(B[9]), .in_2(A[9]), .B_Invert(B_Invert), .ALU_Op(2'b10));  // open: Set
  _1_Bit_ALU u_1_bit_alu_11 (
    .C_in(n1_bit_alu_10_c_out), .Less(1'b0), .ALU_Output(ALU_Output[10]), .C_out(n1_bit_alu_11_c_out),
    .in_1(B[10]), .in_2(A[10]), .B_Invert(B_Invert), .ALU_Op(2'b10));  // open: Set
  _1_Bit_ALU u_1_bit_alu_12 (
    .C_in(n1_bit_alu_11_c_out), .Less(1'b0), .ALU_Output(ALU_Output[11]), .C_out(n1_bit_alu_12_c_out),
    .in_1(B[11]), .in_2(A[11]), .B_Invert(B_Invert), .ALU_Op(2'b10));  // open: Set
  _1_Bit_ALU u_1_bit_alu_13 (
    .C_in(n1_bit_alu_12_c_out), .Less(1'b0), .ALU_Output(ALU_Output[12]), .C_out(n1_bit_alu_13_c_out),
    .in_1(B[12]), .in_2(A[12]), .B_Invert(B_Invert), .ALU_Op(2'b10));  // open: Set
  _1_Bit_ALU u_1_bit_alu_14 (
    .C_in(n1_bit_alu_13_c_out), .Less(1'b0), .ALU_Output(ALU_Output[13]), .C_out(n1_bit_alu_14_c_out),
    .in_1(B[13]), .in_2(A[13]), .B_Invert(B_Invert), .ALU_Op(2'b10));  // open: Set
  _1_Bit_ALU u_1_bit_alu_15 (
    .C_in(n1_bit_alu_14_c_out), .Less(1'b0), .ALU_Output(ALU_Output[14]), .C_out(n1_bit_alu_15_c_out),
    .in_1(B[14]), .in_2(A[14]), .B_Invert(B_Invert), .ALU_Op(2'b10));  // open: Set
  _1_Bit_ALU u_1_bit_alu_16 (
    .C_in(n1_bit_alu_15_c_out), .Less(1'b0), .ALU_Output(ALU_Output[15]), .C_out(C_Out), .in_1(B[15]),
    .in_2(A[15]), .B_Invert(B_Invert), .ALU_Op(2'b10), .Set(n1_bit_alu_16_set));
  xor xor_1 (Overflow_Flag, n1_bit_alu_15_c_out, C_Out);
  nor nor_1 (Zero_Flag, ALU_Output[0], ALU_Output[1], ALU_Output[2], ALU_Output[3], ALU_Output[4], ALU_Output[5], ALU_Output[6], ALU_Output[7], ALU_Output[8], ALU_Output[9], ALU_Output[10], ALU_Output[11], ALU_Output[12], ALU_Output[13], ALU_Output[14], ALU_Output[15]);

  // Notes on the sheet:
  //   C_In
  //   Set
endmodule

// sign
module sign_handler (
  input  [31:0] number,
  input  [11:0] exp,
  input  sign,
  output [31:0] out_4
);

  wire bitfinder_1_found;
  wire [31:0] multiplexer_1_out, negator_1_out;

  BitFinder #(.width(12)) bitfinder_1 (.in(exp), .found(bitfinder_1_found));  // open: index
  Negator #(.width(32)) negator_1 (.in(number), .out(negator_1_out));
  Multiplexer #(.width(32)) multiplexer_1 (
    .in0(number), .in1(negator_1_out), .out(multiplexer_1_out), .sel(sign), .en(1'b1));
  Multiplexer #(.width(32)) multiplexer_2 (
    .in0({32{1'b0}}), .in1(multiplexer_1_out), .out(out_4), .sel(bitfinder_1_found), .en(1'b1));
endmodule

// Exp
module exponent_handler (
  input  [11:0] X,
  input  [11:0] Y,
  output Decision__if_x___y,
  output Decision__If_X_Y,
  output [11:0] Larger_Exponent,
  output [11:0] Difference
);

  wire comparator_1_eq;
  wire [11:0] negator_1_out;
  wire [12:0] bit_extender_1_out, bit_extender_2_out;
  wire [15:0] n16_bit_alu_1_alu_output;

  assign bit_extender_1_out = {{1{1'b0}}, X};  // Bit_Extender bit_extender_1
  assign bit_extender_2_out = {{1{1'b0}}, Y};  // Bit_Extender bit_extender_2
  Comparator #(.width(13)) comparator_1 (
    .a(bit_extender_1_out), .b(bit_extender_2_out), .eq(comparator_1_eq), .lt(Decision__If_X_Y));  // open: gt
  _16_Bit_ALU u_16_bit_alu_1 (
    .A({4'b0000, X}), .B({4'b0000, Y}), .ALU_Output(n16_bit_alu_1_alu_output), .B_Invert(1'b1));  // open: Zero_Flag, Overflow_Flag, C_Out
  not not_1 (Decision__if_x___y, comparator_1_eq);
  Multiplexer #(.width(12), .enable("false")) multiplexer_1 (
    .in0(X), .in1(Y), .out(Larger_Exponent), .sel(Decision__If_X_Y));
  Negator #(.width(12)) negator_1 (.in(n16_bit_alu_1_alu_output[11:0]), .out(negator_1_out));
  Multiplexer #(.width(12), .enable("false")) multiplexer_2 (
    .in0(n16_bit_alu_1_alu_output[11:0]), .in1(negator_1_out), .out(Difference), .sel(Decision__If_X_Y));
endmodule
