// Logisim project FP adder.circ as structural Verilog: 2 circuits, main circuit sign handler
module sign_handler (
  input  [11:0] in_1,
  input  [18:0] in_2,
  input  in_3,
  output [18:0] out_4
);

  wire bitfinder_1_found;
  wire [18:0] multiplexer_1_out, negator_1_out;

  BitFinder #(.width(12)) bitfinder_1 (.in(in_1), .found(bitfinder_1_found));  // open: index
  Negator #(.width(19)) negator_1 (.in(in_2), .out(negator_1_out));
  Multiplexer #(.width(19)) multiplexer_1 (
    .in0(in_2), .in1(negator_1_out), .out(multiplexer_1_out), .sel(in_3), .en(1'b1));
  Multiplexer #(.width(19)) multiplexer_2 (
    .in0({19{1'b0}}), .in1(multiplexer_1_out), .out(out_4), .sel(bitfinder_1_found), .en(1'b1));
endmodule

module exponent_handler (
  input  [11:0] in_1,
  input  [11:0] in_2
);

  Comparator #(.width(12)) comparator_1 (.a(in_1), .b(in_2));  // open: gt, eq, lt
endmodule
