// Logisim project FPAdder.circ as structural Verilog: 2 circuits, main circuit main
module main (
  input  [31:0] A,
  input  [31:0] B,
  output [31:0] Y
);

  FPAdder FPAdder (.A(A), .B(B), .Y(Y));
endmodule

module FPAdder (
  input  [31:0] A,
  input  [31:0] B,
  output [31:0] Y
);

  wire Fraction_Adder_zero_flag;
  wire [11:0] Fraction_Adder_exponent, Normalizer_normalized_exponent;
  wire [31:0] Fraction_Adder_sum, Normalizer_2_normalized_fraction, Normalizer_2_normalized_fraction_2,
       Normalizer_normalized_fraction, Rounder_out_2;

  Exponent_main Fraction_Adder (
    .A(A), .B(B), .Sum(Fraction_Adder_sum), .Exponent(Fraction_Adder_exponent),
    .Sign_bit(Normalizer_2_normalized_fraction_2[31]), .Zero_Flag(Fraction_Adder_zero_flag));
  Normalizer_main Normalizer (
    .Fraction(Fraction_Adder_sum), .Exponent(Fraction_Adder_exponent),
    .Normalized_Fraction(Normalizer_normalized_fraction), .Normalized_Exponent(Normalizer_normalized_exponent));
  Main Rounder (.in_1(Normalizer_normalized_fraction), .out_2(Rounder_out_2));
  Normalizer_main Normalizer_2 (
    .Fraction(Rounder_out_2), .Exponent(Normalizer_normalized_exponent),
    .Normalized_Fraction({Normalizer_2_normalized_fraction[31:26], Normalizer_2_normalized_fraction_2[18:0], Normalizer_2_normalized_fraction[6:0]}),
    .Normalized_Exponent(Normalizer_2_normalized_fraction_2[30:19]));
  Multiplexer #(.width(32), .enable("false")) multiplexer_1 (
    .in0({32{1'b0}}), .in1(Normalizer_2_normalized_fraction_2), .out(Y), .sel(Fraction_Adder_zero_flag));
endmodule
