// Logisim project Normalizer.circ as structural Verilog: 3 circuits, main circuit main
// Normalizer
module main (
  input  [31:0] Fraction,
  input  [11:0] Exponent,
  output [31:0] Normalized_Fraction,
  output [11:0] Normalized_Exponent
);

  wire [4:0] bitfinder_1_index, subtractor_1_out;
  wire [11:0] bit_extender_3_out, incrementor_1_incremented_output;
  wire [15:0] bit_extender_1_out, bit_extender_2_out, n16_bit_alu_1_p5;
  wire [31:0] demultiplexer_1_out0, demultiplexer_1_out1, demultiplexer_1_out2, demultiplexer_1_out3,
       right_shift_1_shifted_output, right_shift_2_shifted_output, shifter_1_out;

  assign bit_extender_1_out = {{4{1'b0}}, Exponent};  // Bit_Extender bit_extender_1
  Demultiplexer #(.select(2), .width(32), .enable("false")) demultiplexer_1 (
    .out0(demultiplexer_1_out0), .out1(demultiplexer_1_out1), .out2(demultiplexer_1_out2),
    .out3(demultiplexer_1_out3), .in(Fraction), .sel(Fraction[27:26]));
  Incrementor incrementor_1 (.Input_to_increment(Exponent), .Incremented_output(incrementor_1_incremented_output));
  assign bit_extender_2_out = {{11{1'b0}}, subtractor_1_out};  // Bit_Extender bit_extender_2
  Right_shift right_shift_1 (.Input_to_shift(demultiplexer_1_out3), .Shifted_output(right_shift_1_shifted_output));
  Right_shift right_shift_2 (.Input_to_shift(demultiplexer_1_out2), .Shifted_output(right_shift_2_shifted_output));
  BitFinder #(.width(32), .\type ("high1")) bitfinder_1 (
    .in(demultiplexer_1_out0), .index(bitfinder_1_index));  // open: found
  // _16_Bit_ALU 16_bit_alu_1: pin names not known; wires that end beside it: bit_extender_1_out, bit_extender_2_out, 1'b1, 2'b10, n16_bit_alu_1_p5
  Subtractor #(.width(5)) subtractor_1 (
    .a(5'b11010), .b(bitfinder_1_index), .out(subtractor_1_out), .bin(1'b0));  // open: bout
  Bit_Extender #(.in_width(16), .out_width(12)) bit_extender_3 (.in(n16_bit_alu_1_p5), .out(bit_extender_3_out));
  Shifter #(.width(32)) shifter_1 (.in(demultiplexer_1_out0), .\dist (subtractor_1_out), .out(shifter_1_out));
  Multiplexer #(.select(2), .width(32), .enable("false")) multiplexer_1 (
    .in0(shifter_1_out), .in1(demultiplexer_1_out1), .in2(right_shift_2_shifted_output),
    .in3(right_shift_1_shifted_output), .out(Normalized_Fraction), .sel(Fraction[27:26]));
  Multiplexer #(.select(2), .width(12), .enable("false")) multiplexer_2 (
    .in0(bit_extender_3_out), .in1(Exponent), .in2(incrementor_1_incremented_output),
    .in3(incrementor_1_incremented_output), .out(Normalized_Exponent), .sel(Fraction[27:26]));
endmodule

// SHR
module Right_shift (
  input  [31:0] Input_to_shift,
  output [31:0] Shifted_output
);

  Shifter #(.width(32), .shift("lr")) shifter_1 (.in(Input_to_shift), .\dist (5'b00001), .out(Shifted_output));
endmodule

module Incrementor (
  input  [11:0] Input_to_increment,
  output [11:0] Incremented_output
);

  wire [15:0] bit_extender_1_out, n16_bit_alu_1_p5;

  assign bit_extender_1_out = {{4{1'b0}}, Input_to_increment};  // Bit_Extender bit_extender_1
  // _16_Bit_ALU 16_bit_alu_1: pin names not known; wires that end beside it: bit_extender_1_out, 16'h1, 1'b0, 2'b10, n16_bit_alu_1_p5
  Bit_Extender #(.in_width(16), .out_width(12)) bit_extender_2 (.in(n16_bit_alu_1_p5), .out(Incremented_output));
endmodule
