// Logisim project Rounder.circ as structural Verilog: 1 circuit, main circuit Main
// Rounder
module Main (
  input  [31:0] in_1,
  output [31:0] out_2
);

  wire n7408_1__3__1y, n7432_1__3__1y, n7432_1__6__2y, n7432_1__8__3y, n7432_1__11__4y, n7432_2__3__1y,
       n7432_2__6__2y;
  wire [31:0] main_1_output;

  _32_Bit_ALU_main main_1 (.Input1(in_1), .Input2(32'h80), .c(3'b100), .Output(main_1_output));  // open: out_5
  _7432 u_7432_1 (
    ._1__1A(in_1[0]), ._2__1B(in_1[1]), ._3__1Y(n7432_1__3__1y), ._4__2A(n7432_1__3__1y), ._5__2B(in_1[2]),
    ._6__2Y(n7432_1__6__2y), ._7__GND(1'b0), ._14__Vcc(1'b1), ._13__4B(n7432_1__6__2y), ._12__4A(in_1[3]),
    ._11__4Y(n7432_1__11__4y), ._10__3B(n7432_1__11__4y), ._9__3A(in_1[4]), ._8__3Y(n7432_1__8__3y));
  _7432 u_7432_2 (
    ._1__1A(n7432_1__8__3y), ._2__1B(in_1[5]), ._3__1Y(n7432_2__3__1y), ._4__2A(n7432_2__3__1y),
    ._5__2B(in_1[7]), ._6__2Y(n7432_2__6__2y), ._7__GND(1'b0), ._14__Vcc(1'b1));  // open: _13__4B, _12__4A, _11__4Y, _10__3B, _9__3A, _8__3Y
  _7408 u_7408_1 (
    ._1__1A(n7432_2__6__2y), ._2__1B(in_1[6]), ._3__1Y(n7408_1__3__1y), ._7__GND(1'b0), ._14__Vcc(1'b1));  // open: _4__2A, _5__2B, _6__2Y, _13__4B, _12__4A, _11__4Y, _10__3B, _9__3A, _8__3Y
  Multiplexer #(.width(32), .enable("false")) multiplexer_1 (
    .in0({in_1[31:7], {7{1'b0}}}), .in1(main_1_output), .out(out_2), .sel(n7408_1__3__1y));

  // Notes on the sheet:
  //   Round Up
  //   R
  //   G
  //   L
  //   S
  //   Truncate
  //   G.(L+S+R)
endmodule
