// Logisim project fraction_allignment.circ as structural Verilog: 1 circuit, main circuit main
module main (
  input  [31:0] Smaller_number,
  input  [11:0] Larger_Exp,
  input  [11:0] Exponent_difference,
  output [31:0] Modified_number
);

  wire [19:19] shifter_1_out;

  Shifter #(.width(20), .shift("lr")) shifter_1 (
    .in({1'b1, Smaller_number[18:0]}), .\dist (Exponent_difference[4:0]),
    .out({shifter_1_out[19], Modified_number[18:0]}));

  assign Modified_number[31:19] = {Smaller_number[31], Larger_Exp};
endmodule
